# Fritzing sketch Circuit Diagram (saved by Fritzing 0.9.3b)
breadboards: 1

parts:
  Componente1 = Arduino Uno (Rev3)
  LCD1 = LCD screen
  S1 = Pushbutton [package="[THT]"]
  J1 = Piezo Speaker
  R2 = Trimmer Potentiometer [maximum_resistance=10kΩ package=THT]

nets:
  N1: Componente1.D8, LCD1.E
  N2: Componente1.D9_PWM, LCD1.DB4
  N3: Componente1.D10_PWM/SS, LCD1.DB5
  N4: Componente1.D11_PWM/MOSI, LCD1.DB6
  N5: Componente1.D12/MISO, LCD1.DB7
  N6: Componente1.D5_PWM, J1.pin2
  N7: Componente1.D6_PWM, S1.Pin_1, S1.Pin_2
  N8: Componente1.D7, LCD1.RS
  5V: Componente1.5V, LCD1.VDD, LCD1.LED+, R2.leg1
  GND: Componente1.GND, LCD1.VSS, LCD1.R/W, LCD1.LED-, S1.Pin_3, S1.Pin_4, J1.pin1, R2.leg2
  N9: LCD1.V0, R2.wiper
